// Logisim project TP6_ORGA_2.circ as structural Verilog: 2 circuits, main circuit main
module main (
);

  wire alu_1_cout, alu_1_zero, clock_1_out, clock_2_out, clock_3_out, clock_4_out, clock_5_out, clock_6_out,
       clock_7_out;
  wire [7:0] ACC_q, alu_1_salida, B_q, multiplexer_1_out;
  wire [11:0] adder_1_out, bit_extender_1_out, MAR_q, PC_q;
  wire [15:0] IR_q, MDR_q, Memoria_dout, rom_1_data, Unidad_De_Control_data;

  Register #(.width(12)) PC (.D(adder_1_out), .clk(clock_1_out), .Q(PC_q));  // open: en, clr
  Clock clock_1 (.out(clock_1_out));
  Adder #(.width(12)) adder_1 (.a(PC_q), .b(12'h1), .out(adder_1_out));  // open: cin, cout
  ROM #(.addrWidth(12), .dataWidth(16)) rom_1 (.addr(PC_q), .data(rom_1_data));
  Register #(.width(16)) MDR (.D(rom_1_data), .clk(clock_2_out), .Q(MDR_q));  // open: en, clr
  Clock clock_2 (.out(clock_2_out));
  Register #(.width(16)) IR (.D(MDR_q), .clk(clock_3_out), .Q(IR_q));  // open: en, clr
  Clock clock_3 (.out(clock_3_out));
  Register #(.width(12)) MAR (.D(IR_q[11:0]), .clk(clock_4_out), .Q(MAR_q));  // open: en, clr
  Clock clock_4 (.out(clock_4_out));
  ROM #(.addrWidth(4), .dataWidth(16)) Unidad_De_Control (.addr(IR_q[15:12]), .data(Unidad_De_Control_data));
  RAM #(.addrWidth(12), .dataWidth(16)) Memoria (
    .addr(MAR_q), .clk(clock_5_out), .dout(Memoria_dout));  // open: we, oe, din
  Clock clock_5 (.out(clock_5_out));
  Bit_Extender #(.in_width(16), .out_width(12), .\type ("zero")) bit_extender_1 (
    .in(Unidad_De_Control_data), .out(bit_extender_1_out));
  Register C ();  // open: D, en, clk, Q, clr
  Multiplexer #(.width(8)) multiplexer_1 (
    .in0(alu_1_salida), .in1(Memoria_dout[7:0]), .out(multiplexer_1_out));  // open: sel
  Register ACC (.D(multiplexer_1_out), .clk(clock_6_out), .Q(ACC_q));  // open: en, clr
  Clock clock_6 (.out(clock_6_out));
  Register B (.D(Memoria_dout[7:0]), .clk(clock_7_out), .Q(B_q));  // open: en, clr
  Clock clock_7 (.out(clock_7_out));
  ALU alu_1 (.B(B_q), .A(ACC_q), .Zero(alu_1_zero), .Salida(alu_1_salida), .Cout(alu_1_cout));  // open: Selector, Cin

  // Notes on the sheet:
  //   contents of Unidad_De_Control (hex, n*v repeats v):
  //   0 1 10 11 100 101 110 111 1000 1001
endmodule

module ALU (
  input  [2:0] Selector,
  input  [7:0] B,
  input  [7:0] A,
  input  Cin,
  output Zero,
  output [7:0] Salida,
  output Cout
);

  wire and_1_out, and_2_out, and_3_out, and_4_out, and_5_out, and_6_out, and_7_out, and_8_out, and_9_out,
       and_10_out, and_11_out, and_12_out, and_13_out, and_14_out, and_15_out, and_16_out, and_17_out,
       and_18_out, and_19_out, and_20_out, and_21_out, and_22_out, and_23_out, and_24_out, nand_1_out,
       nand_2_out, nand_3_out, nand_4_out, nand_5_out, nand_6_out, nand_7_out, nand_8_out, not_1_out,
       not_2_out, or_1_out, or_2_out, or_3_out, or_4_out, or_5_out, or_6_out, or_7_out, or_8_out, or_9_out,
       or_10_out, or_11_out, or_12_out, or_13_out, or_14_out, or_15_out, or_18_out, or_19_out, or_20_out,
       or_21_out, or_22_out, or_23_out, or_24_out, xor_1_out, xor_2_out, xor_3_out, xor_4_out, xor_5_out,
       xor_6_out, xor_7_out, xor_8_out, xor_9_out, xor_10_out, xor_11_out, xor_12_out, xor_13_out,
       xor_14_out, xor_15_out, xor_16_out, xor_17_out, xor_18_out, xor_19_out, xor_20_out, xor_21_out,
       xor_22_out, xor_23_out, xor_24_out, xor_25_out, xor_26_out, xor_27_out, xor_28_out, xor_29_out,
       xor_30_out, xor_31_out, xor_32_out;
  wire [7:0] and_25_out, and_33_out, and_41_out, and_49_out, and_57_out;

  and and_1 (and_1_out, A[0], B[0]);
  and and_2 (and_2_out, A[1], B[1]);
  and and_3 (and_3_out, A[2], B[2]);
  and and_4 (and_4_out, A[3], B[3]);
  and and_5 (and_5_out, A[4], B[4]);
  and and_6 (and_6_out, A[5], B[5]);
  and and_7 (and_7_out, A[6], B[6]);
  and and_8 (and_8_out, A[7], B[7]);
  or or_1 (or_1_out, A[0], B[0]);
  or or_2 (or_2_out, A[1], B[1]);
  or or_3 (or_3_out, A[2], B[2]);
  or or_4 (or_4_out, A[3], B[3]);
  or or_5 (or_5_out, A[4], B[4]);
  or or_6 (or_6_out, A[5], B[5]);
  or or_7 (or_7_out, A[6], B[6]);
  or or_8 (or_8_out, A[7], B[7]);
  nand nand_1 (nand_1_out, A[0], B[0]);
  nand nand_2 (nand_2_out, A[1], B[1]);
  nand nand_3 (nand_3_out, A[2], B[2]);
  nand nand_4 (nand_4_out, A[3], B[3]);
  nand nand_5 (nand_5_out, A[4], B[4]);
  nand nand_6 (nand_6_out, A[5], B[5]);
  nand nand_7 (nand_7_out, A[6], B[6]);
  nand nand_8 (nand_8_out, A[7], B[7]);
  xor xor_1 (xor_1_out, A[0], B[0]);
  xor xor_2 (xor_2_out, A[1], B[1]);
  xor xor_3 (xor_3_out, A[2], B[2]);
  xor xor_4 (xor_4_out, A[3], B[3]);
  xor xor_5 (xor_5_out, A[4], B[4]);
  xor xor_6 (xor_6_out, A[5], B[5]);
  xor xor_7 (xor_7_out, A[6], B[6]);
  xor xor_8 (xor_8_out, A[7], B[7]);
  xor xor_9 (xor_9_out, Cin, B[0]);
  xor xor_10 (xor_10_out, Cin, B[1]);
  xor xor_11 (xor_11_out, Cin, B[2]);
  xor xor_12 (xor_12_out, Cin, B[3]);
  xor xor_13 (xor_13_out, Cin, B[4]);
  xor xor_14 (xor_14_out, Cin, B[5]);
  xor xor_15 (xor_15_out, Cin, B[6]);
  xor xor_16 (xor_16_out, Cin, B[7]);
  xor xor_17 (xor_17_out, A[0], xor_9_out);
  xor xor_18 (xor_18_out, A[1], xor_10_out);
  xor xor_19 (xor_19_out, A[2], xor_11_out);
  xor xor_20 (xor_20_out, A[3], xor_12_out);
  xor xor_21 (xor_21_out, A[4], xor_13_out);
  xor xor_22 (xor_22_out, A[5], xor_14_out);
  xor xor_23 (xor_23_out, A[6], xor_15_out);
  xor xor_24 (xor_24_out, A[7], xor_16_out);
  xor xor_25 (xor_25_out, xor_17_out, Cin);
  and and_9 (and_9_out, Cin, xor_17_out);
  and and_10 (and_10_out, xor_9_out, A[0]);
  xor xor_26 (xor_26_out, xor_18_out, or_9_out);
  and and_11 (and_11_out, or_9_out, xor_18_out);
  and and_12 (and_12_out, xor_10_out, A[1]);
  xor xor_27 (xor_27_out, xor_19_out, or_10_out);
  and and_13 (and_13_out, or_10_out, xor_19_out);
  and and_14 (and_14_out, xor_11_out, A[2]);
  xor xor_28 (xor_28_out, xor_20_out, or_11_out);
  and and_15 (and_15_out, or_11_out, xor_20_out);
  and and_16 (and_16_out, xor_12_out, A[3]);
  xor xor_29 (xor_29_out, xor_21_out, or_12_out);
  and and_17 (and_17_out, or_12_out, xor_21_out);
  and and_18 (and_18_out, xor_13_out, A[4]);
  xor xor_30 (xor_30_out, xor_22_out, or_13_out);
  and and_19 (and_19_out, or_13_out, xor_22_out);
  and and_20 (and_20_out, xor_14_out, A[5]);
  xor xor_31 (xor_31_out, xor_23_out, or_14_out);
  and and_21 (and_21_out, or_14_out, xor_23_out);
  and and_22 (and_22_out, xor_15_out, A[6]);
  xor xor_32 (xor_32_out, xor_24_out, or_15_out);
  and and_23 (and_23_out, or_15_out, xor_24_out);
  and and_24 (and_24_out, xor_16_out, A[7]);
  or or_9 (or_9_out, and_9_out, and_10_out);
  or or_10 (or_10_out, and_11_out, and_12_out);
  or or_11 (or_11_out, and_13_out, and_14_out);
  or or_12 (or_12_out, and_15_out, and_16_out);
  or or_13 (or_13_out, and_17_out, and_18_out);
  or or_14 (or_14_out, and_19_out, and_20_out);
  or or_15 (or_15_out, and_21_out, and_22_out);
  or or_16 (Cout, and_23_out, and_24_out);
  not not_1 (not_1_out, Selector[1]);
  not not_2 (not_2_out, Selector[2]);
  and and_25 (and_25_out[0], Selector[0], not_1_out, not_2_out, and_1_out);
  and and_26 (and_25_out[1], Selector[0], not_1_out, not_2_out, and_2_out);
  and and_27 (and_25_out[2], Selector[0], not_1_out, not_2_out, and_3_out);
  and and_28 (and_25_out[3], Selector[0], not_1_out, not_2_out, and_4_out);
  and and_29 (and_25_out[4], Selector[0], not_1_out, not_2_out, and_5_out);
  and and_30 (and_25_out[5], Selector[0], not_1_out, not_2_out, and_6_out);
  and and_31 (and_25_out[6], Selector[0], not_1_out, not_2_out, and_7_out);
  and and_32 (and_25_out[7], Selector[0], not_1_out, not_2_out, and_8_out);
  and and_33 (and_33_out[0], Selector[0], not_1_out, not_2_out, or_1_out);
  and and_34 (and_33_out[1], Selector[0], not_1_out, not_2_out, or_2_out);
  and and_35 (and_33_out[2], Selector[0], not_1_out, not_2_out, or_3_out);
  and and_36 (and_33_out[3], Selector[0], not_1_out, not_2_out, or_4_out);
  and and_37 (and_33_out[4], Selector[0], not_1_out, not_2_out, or_5_out);
  and and_38 (and_33_out[5], Selector[0], not_1_out, not_2_out, or_6_out);
  and and_39 (and_33_out[6], Selector[0], not_1_out, not_2_out, or_7_out);
  and and_40 (and_33_out[7], Selector[0], not_1_out, not_2_out, or_8_out);
  and and_41 (and_41_out[0], Selector[0], Selector[1], not_1_out, nand_1_out);
  and and_42 (and_41_out[1], Selector[0], Selector[0], not_2_out, nand_2_out);
  and and_43 (and_41_out[2], Selector[0], Selector[1], not_2_out, nand_3_out);
  and and_44 (and_41_out[3], Selector[0], Selector[1], not_2_out, nand_4_out);
  and and_45 (and_41_out[4], Selector[0], Selector[1], not_2_out, nand_5_out);
  and and_46 (and_41_out[5], Selector[0], Selector[1], not_2_out, nand_6_out);
  and and_47 (and_41_out[6], Selector[0], Selector[1], not_2_out, nand_7_out);
  and and_48 (and_41_out[7], Selector[0], Selector[1], not_2_out, nand_8_out);
  and and_49 (and_49_out[0], Selector[0], Selector[1], not_2_out, xor_1_out);
  and and_50 (and_49_out[1], Selector[0], Selector[1], not_2_out, xor_2_out);
  and and_51 (and_49_out[2], Selector[0], Selector[1], not_2_out, xor_3_out);
  and and_52 (and_49_out[3], Selector[0], Selector[1], not_2_out, xor_4_out);
  and and_53 (and_49_out[4], Selector[0], Selector[1], not_2_out, xor_5_out);
  and and_54 (and_49_out[5], Selector[0], Selector[1], not_2_out, xor_6_out);
  and and_55 (and_49_out[6], Selector[0], Selector[1], not_2_out, xor_7_out);
  and and_56 (and_49_out[7], Selector[0], Selector[1], not_2_out, xor_8_out);
  and and_57 (and_57_out[0], Selector[0], not_1_out, Selector[2], xor_25_out);
  and and_58 (and_57_out[1], Selector[0], not_1_out, Selector[2], xor_26_out);
  and and_59 (and_57_out[2], Selector[0], not_1_out, Selector[2], xor_27_out);
  and and_60 (and_57_out[3], Selector[0], not_1_out, Selector[2], xor_28_out);
  and and_61 (and_57_out[4], Selector[0], not_1_out, Selector[2], xor_29_out);
  and and_62 (and_57_out[5], Selector[0], not_1_out, Selector[2], xor_30_out);
  and and_63 (and_57_out[6], Selector[0], not_1_out, Selector[2], xor_31_out);
  and and_64 (and_57_out[7], Selector[0], not_1_out, Selector[2], xor_32_out);
  assign Salida = and_25_out | and_33_out | and_41_out | and_49_out | and_57_out;  // OR_Gate or_17, 8 bits wide
  or or_18 (or_18_out, Salida[0], Salida[1]);
  or or_19 (or_19_out, Salida[2], Salida[3]);
  or or_20 (or_20_out, Salida[4], Salida[5]);
  or or_21 (or_21_out, Salida[6], Salida[7]);
  or or_22 (or_22_out, or_18_out, or_19_out);
  or or_23 (or_23_out, or_20_out, or_21_out);
  or or_24 (or_24_out, or_22_out, or_23_out);
  not not_3 (Zero, or_24_out);
endmodule
